# Fritzing sketch LED Thinggy (saved by Fritzing 0.9.2b)
circuit board: 5.92404cm x 5.3453cm
breadboards: 1

parts:
  R1 = Resistor [tolerance=±5% resistance=220 package=THT]
  R2 = Resistor [tolerance=±5% resistance=220 package=THT]
  R3 = Resistor [tolerance=±5% resistance=220 package=THT]
  R4 = Resistor [tolerance=±5% resistance=220 package=THT]
  R5 = Resistor [tolerance=±5% resistance=220 package=THT]
  R6 = Resistor [tolerance=±5% resistance=220 package=THT]
  R7 = Resistor [tolerance=±5% resistance=220 package=THT]
  J1 = female pin header, 8 pins [form="♀ (female)"]
  LED1 = LED - 5mm [color="Red (633nm)" package="5 mm [THT]"]
  LED2 = LED - 5mm [color="Red (633nm)" package="5 mm [THT]"]
  LED3 = LED - 5mm [color="Red (633nm)" package="5 mm [THT]"]
  LED4 = LED - 5mm [color="Red (633nm)" package="5 mm [THT]"]
  LED5 = LED - 5mm [color="Red (633nm)" package="5 mm [THT]"]
  LED6 = LED - 5mm [color="Red (633nm)" package="5 mm [THT]"]
  LED7 = LED - 5mm [color="Red (633nm)" package="5 mm [THT]"]

nets:
  N1: R1.Pin_0, LED1.anode
  N2: R1.Pin_1, J1.pin1
  N3: R2.Pin_0, LED2.anode
  N4: R2.Pin_1, J1.pin2
  N5: R3.Pin_0, LED6.anode
  N6: R3.Pin_1, J1.pin3
  N7: R4.Pin_0, LED7.anode
  N8: R4.Pin_1, J1.pin4
  N9: R5.Pin_0, LED3.anode
  N10: R5.Pin_1, J1.pin5
  N11: R6.Pin_0, LED4.anode
  N12: R6.Pin_1, J1.pin6
  N13: R7.Pin_0, LED5.anode
  N14: R7.Pin_1, J1.pin7
  N15: J1.pin8, LED1.cathode, LED2.cathode, LED3.cathode, LED4.cathode, LED5.cathode, LED6.cathode, LED7.cathode

notes:
  Rainbow LED Board
